# Fritzing sketch tricycle (saved by Fritzing 0.9.3b)
breadboards: 1

parts:
  Componente1 = Arduino Uno (Rev3)
  Componente2 = Bluetooth HC-05 Macho
  BAT1 = Battery Holders [package=battery-aa-kit]
  BAT2 = Battery Holders [package=battery-aa-kit]
  BAT3 = Battery Holders [package=battery-aa-kit]
  BAT4 = Battery Holders [package=battery-aa-kit]
  IC2 = L293D [package=THT]
  M1 = DC Motor
  J1 = Basic Servo

nets (from the schematic view):
  N1: Componente1.D9_PWM, J1.pulse
  N2: Componente1.D10_PWM/SS, IC2.In_1
  N3: Componente1.D11_PWM/MOSI, IC2.In_2
  N4: Componente1.D0/RX, Componente2.RXD
  VCC: Componente1.5V, Componente2.VCC, BAT1.+, IC2.Enable_1, IC2.+Vmotor, IC2.+V, J1.vcc
  GND: Componente1.GND, Componente2.GND, BAT4.-, IC2.0V, IC2.Enable_2, J1.gnd
  N5: BAT1.-, BAT2.+
  N6: BAT2.-, BAT3.+
  N7: BAT3.-, BAT4.+
  N8: IC2.Out_1_(_Controlled_by_Enable_1_), M1.pin_2
  N9: IC2.Out_2_(_Controlled_by_Enable_1_), M1.pin_1

// code stored in the sketch: carrinho.ino
/* Simple and cheap DIY arduino rc tricycle controlled by smartphone 

 modified 31 March 2017
 by lcgamboa@yahoo.com
 https://www.youtube.com/watch?v=XjhdBfRUhjk
*/

//code for arduino uno

#include <Servo.h>

Servo myservo;  // create servo object to control a servo

#define center 94 //angle to align center position

void setup() {

  pinMode(10, OUTPUT); //Foward H bridge
  pinMode(11, OUTPUT); //Backward H bridge
  
  myservo.attach(9);  // Direction servo
  myservo.write(center);

  digitalWrite(10, LOW);
  digitalWrite(11, LOW);
            
  Serial.begin(19200); //Bluetooth connection
}

void loop() {

  if (Serial.available() > 0) { //if receveid bluetooth command
     unsigned char cmd = Serial.read();

     switch(cmd)
     {
       case 'w'://frente - foward
         digitalWrite(10, HIGH);
         digitalWrite(11, LOW);
         break; 
       case 'r'://parar - stop
         digitalWrite(10, LOW);
         digitalWrite(11, LOW);
         break; 
       case 's'://trás - backward
         digitalWrite(10, LOW);
         digitalWrite(11, HIGH);
         break; 
       case 'd'://direita  - right
         myservo.write(140); //angle in degrees
         break; 
       case 'a'://esquerda  -left
         myservo.write(40); //angle in degrees
         break; 
       case 'q'://centro  -center
         myservo.write(center); 
         break; 
       default:
         break; 
     }

  }
                
    
}
