# Fritzing sketch tricycle_pic (saved by Fritzing 0.9.3b)
breadboards: 1

parts:
  XTAL1 = Crystal [frequency="16 Mhz" package=THT]
  C1 = Ceramic Capacitor [capacitance=100nF package="200 mil [THT, multilayer]"]
  C1_2 = Ceramic Capacitor [capacitance=100nF package="200 mil [THT, multilayer]"]
  U1 = PIC-ICSP [package=molex-1x6]
  PIC_16F877A1 = PIC 16F877A [package=THT]
  Componente1 = Bluetooth HC-05 Macho  # not connected

nets:
  N1: XTAL1.pin_0, C1_2.0, PIC_16F877A1.OSC2/CLKOUT
  N2: C1.0, PIC_16F877A1.OSC1/CLKIN
  N3: C1_2.1, U1.GND, PIC_16F877A1.VSS#11
  N4: U1.PGC, PIC_16F877A1.RB6
  N5: U1.PGD, PIC_16F877A1.RB7
  N6: U1.VCC, PIC_16F877A1.VDD#10
  N7: U1.VPP, PIC_16F877A1.MCLR
